# Fritzing sketch robot_schematic (saved by Fritzing 0.9.3b)
breadboards: 1

parts:
  IC1 = L293D [package=THT]
  Left_Motor = DC Motor
  Part1 = Arduino Uno (Rev3)
  Right_Motor = DC Motor
  IR1 = TSOP312.., 314.. [package=THT]
  C1 = Electrolytic Capacitor [capacitance=1µF package="100 mil [THT, electrolytic]"]
  J1 = Basic Servo
  LED1 = LED - 5mm [color="Yellow (595nm)" package="5 mm [THT]"]
  LED2 = LED - 5mm [color="Yellow (595nm)" package="5 mm [THT]"]
  R1 = Resistor [tolerance=±5% resistance=220 package=THT]
  LED3 = LED - 5mm [color="Red (633nm)" package="5 mm [THT]"]
  R2 = Resistor [tolerance=±5% resistance=220 package=THT]
  LED4 = LED - 5mm [color="White (4500K)" package="5 mm [THT]"]
  R3 = Resistor [tolerance=±5% resistance=220 package=THT]
  LED5 = LED - 5mm [color="White (4500K)" package="5 mm [THT]"]
  R4 = Photocell (LDR) [package=THT]
  R5 = Resistor [tolerance=±5% resistance=220 package=THT]

nets:
  5V: IC1.Enable_1, IC1.+Vmotor, IC1.Enable_2, IC1.+V, Part1.5V, J1.vcc, R5.Pin_1
  N1: IC1.In_1, Part1.D12/MISO
  N2: IC1.Out_1_(_Controlled_by_Enable_1_), Left_Motor.pin_2
  GND: IC1.0V, Part1.GND, IR1.GND, IR1.Vs, C1.-, C1.+, J1.gnd, LED1.cathode, LED2.cathode, R1.Pin_0, LED3.cathode, R2.Pin_1, LED4.cathode, R3.Pin_1, LED5.cathode, R4.pin_0
  N3: IC1.Out_2_(_Controlled_by_Enable_1_), Left_Motor.pin_1
  N4: IC1.In_2, Part1.D11_PWM/MOSI
  N5: IC1.In_3, Part1.D9_PWM
  N6: IC1.Out_3_(_Controlled_by_Enable_2_), Right_Motor.pin_1
  N7: IC1.Out_4_(_Controlled_by_Enable_2_), Right_Motor.pin_2
  N8: IC1.In_4, Part1.D10_PWM/SS
  N9: Part1.A0, R4.pin_1, R5.Pin_0
  N10: Part1.D8, R2.Pin_0, LED4.anode
  N11: Part1.D13/SCK, R3.Pin_0, LED5.anode
  N12: Part1.D2, IR1.Data
  N13: Part1.D3_PWM, J1.pulse
  N14: Part1.D5_PWM, LED1.anode
  N15: Part1.D6_PWM, LED2.anode
  N16: Part1.D7, R1.Pin_1, LED3.anode
